// Logisim project 1 bit register.circ as structural Verilog: 1 circuit, main circuit main
module main (
  input  Enable,
  input  Cin,
  input  Input,
  input  Select1,
  input  Select2,
  output Cout,
  output Output
);

  wire adder_1_out, main_1_out_9;

  _4_main main_1 (
    .in_1(1'b0), .in_2(adder_1_out), .in_3(adder_1_out), .in_4(Input), .out_9(main_1_out_9), .in_5(Select1),
    .in_6(Select2));  // open: out_7, out_8
  D_Flip_Flop d_ff_1 (.clk(Enable), .D(main_1_out_9), .Q(Output));  // open: Qn, preset, en, reset
  Adder #(.width(1)) adder_1 (.a(Output), .b(Select1), .out(adder_1_out), .cin(Cin), .cout(Cout));
endmodule
