// Logisim project 3 registers.circ as structural Verilog: 1 circuit, main circuit main
module main (
  input  [1:0] FunSel,
  input  [2:0] RegSel,
  input  [1:0] OutASel,
  input  [7:0] Input,
  output [7:0] outA
);

  wire and_1_out, and_2_out, and_3_out, AR_lsb_2, AR_out_13, AR_out_14, AR_out_15, AR_out_16, AR_out_17,
       AR_out_18, AR_out_19, AR_out_20, AR_out_21, Clock_out, main_2_out_7, main_2_out_8, main_3_out_7,
       main_3_out_8, main_4_out_7, main_4_out_8, main_5_out_7, main_5_out_8, main_6_out_7, main_6_out_8,
       main_7_out_7, main_7_out_8, main_8_out_7, main_8_out_8, PC_lsb_2, PC_out_13, PC_out_14, PC_out_15,
       PC_out_16, PC_out_17, PC_out_18, PC_out_19, PC_out_20, PC_out_21, SP_lsb_2, SP_out_13, SP_out_14,
       SP_out_15, SP_out_16, SP_out_17, SP_out_18, SP_out_19;

  Clock Clock (.out(Clock_out));
  and and_1 (and_1_out, Clock_out, RegSel[0]);
  Hex_Digit_Display hex_digit_display_1 (.value(Input[7:4]));  // open: dp
  and and_2 (and_2_out, Clock_out, RegSel[2]);
  and and_3 (and_3_out, Clock_out, RegSel[1]);
  Hex_Digit_Display hex_digit_display_2 (.value(Input[3:0]));  // open: dp
  _8_bit_register_main PC (
    .Select1(FunSel[1]), .Select0(FunSel[0]), .Enable(and_2_out), .LSB_2(PC_lsb_2), .out_13(PC_out_13),
    .out_14(PC_out_14), .out_15(PC_out_15), .out_16(PC_out_16), .out_17(PC_out_17), .out_18(PC_out_18),
    .out_19(PC_out_19), .LSB(Input[0]), .in_5(Input[1]), .in_6(Input[2]), .in_7(Input[3]), .in_8(Input[4]),
    .in_9(Input[5]), .in_10(Input[6]), .in_11(Input[7]), .out_20(PC_out_20), .out_21(PC_out_21));  // open: out_22
  _8_bit_register_main AR (
    .Select1(PC_out_20), .Select0(PC_out_21), .Enable(and_3_out), .LSB_2(AR_lsb_2), .out_13(AR_out_13),
    .out_14(AR_out_14), .out_15(AR_out_15), .out_16(AR_out_16), .out_17(AR_out_17), .out_18(AR_out_18),
    .out_19(AR_out_19), .LSB(Input[0]), .in_5(Input[1]), .in_6(Input[2]), .in_7(Input[3]), .in_8(Input[4]),
    .in_9(Input[5]), .in_10(Input[6]), .in_11(Input[7]), .out_20(AR_out_20), .out_21(AR_out_21));  // open: out_22
  _8_bit_register_main SP (
    .Select1(AR_out_20), .Select0(AR_out_21), .Enable(and_1_out), .LSB_2(SP_lsb_2), .out_13(SP_out_13),
    .out_14(SP_out_14), .out_15(SP_out_15), .out_16(SP_out_16), .out_17(SP_out_17), .out_18(SP_out_18),
    .out_19(SP_out_19), .LSB(Input[0]), .in_5(Input[1]), .in_6(Input[2]), .in_7(Input[3]), .in_8(Input[4]),
    .in_9(Input[5]), .in_10(Input[6]), .in_11(Input[7]));  // open: out_20, out_21, out_22
  _4_main main_1 (
    .in_1(PC_out_19), .in_2(PC_out_19), .in_3(AR_out_19), .in_4(SP_out_19), .out_9(outA[7]),
    .in_5(main_2_out_7), .in_6(main_2_out_8));  // open: out_7, out_8
  _4_main main_2 (
    .out_7(main_2_out_7), .out_8(main_2_out_8), .in_1(PC_out_18), .in_2(PC_out_18), .in_3(AR_out_18),
    .in_4(SP_out_18), .out_9(outA[6]), .in_5(main_3_out_7), .in_6(main_3_out_8));
  _4_main main_3 (
    .out_7(main_3_out_7), .out_8(main_3_out_8), .in_1(PC_out_17), .in_2(PC_out_17), .in_3(AR_out_17),
    .in_4(SP_out_17), .out_9(outA[5]), .in_5(main_4_out_7), .in_6(main_4_out_8));
  _4_main main_4 (
    .out_7(main_4_out_7), .out_8(main_4_out_8), .in_1(PC_out_16), .in_2(PC_out_16), .in_3(AR_out_16),
    .in_4(SP_out_16), .out_9(outA[4]), .in_5(main_5_out_7), .in_6(main_5_out_8));
  _4_main main_5 (
    .out_7(main_5_out_7), .out_8(main_5_out_8), .in_1(PC_out_15), .in_2(PC_out_15), .in_3(AR_out_15),
    .in_4(SP_out_15), .out_9(outA[3]), .in_5(main_6_out_7), .in_6(main_6_out_8));
  _4_main main_6 (
    .out_7(main_6_out_7), .out_8(main_6_out_8), .in_1(PC_out_14), .in_2(PC_out_14), .in_3(AR_out_14),
    .in_4(SP_out_14), .out_9(outA[2]), .in_5(main_7_out_7), .in_6(main_7_out_8));
  _4_main main_7 (
    .out_7(main_7_out_7), .out_8(main_7_out_8), .in_1(PC_out_13), .in_2(PC_out_13), .in_3(AR_out_13),
    .in_4(SP_out_13), .out_9(outA[1]), .in_5(main_8_out_7), .in_6(main_8_out_8));
  _4_main main_8 (
    .out_7(main_8_out_7), .out_8(main_8_out_8), .in_1(PC_lsb_2), .in_2(PC_lsb_2), .in_3(AR_lsb_2),
    .in_4(SP_lsb_2), .out_9(outA[0]), .in_5(OutASel[1]), .in_6(OutASel[0]));
  Hex_Digit_Display hex_digit_display_3 (.value(outA[7:4]));  // open: dp
  Hex_Digit_Display hex_digit_display_4 (.value(outA[3:0]));  // open: dp
endmodule
