// Logisim project 4 registers.circ as structural Verilog: 1 circuit, main circuit main
module main (
  input  [1:0] FunSel,
  input  [3:0] RegSel,
  input  [1:0] OutASel,
  input  [7:0] Input,
  input  [1:0] OutBSel,
  output [7:0] outA,
  output [7:0] outB
);

  wire and_1_out, and_2_out, and_3_out, and_4_out, Clock_out, main_2_out_7, main_2_out_8, main_3_out_7,
       main_3_out_8, main_4_out_7, main_4_out_8, main_5_out_7, main_5_out_8, main_6_out_7, main_6_out_8,
       main_7_out_7, main_7_out_8, main_8_out_7, main_8_out_8, main_10_out_7, main_10_out_8, main_11_out_7,
       main_11_out_8, main_12_out_7, main_12_out_8, main_13_out_7, main_13_out_8, main_14_out_7,
       main_14_out_8, main_15_out_7, main_15_out_8, main_16_out_7, main_16_out_8, R0_lsb_2, R0_out_13,
       R0_out_14, R0_out_15, R0_out_16, R0_out_17, R0_out_18, R0_out_19, R0_out_20, R0_out_21, R1_lsb_2,
       R1_out_13, R1_out_14, R1_out_15, R1_out_16, R1_out_17, R1_out_18, R1_out_19, R1_out_20, R1_out_21,
       R2_lsb_2, R2_out_13, R2_out_14, R2_out_15, R2_out_16, R2_out_17, R2_out_18, R2_out_19, R2_out_20,
       R2_out_21, R3_lsb_2, R3_out_13, R3_out_14, R3_out_15, R3_out_16, R3_out_17, R3_out_18, R3_out_19;

  Clock Clock (.out(Clock_out));
  buf and_1 (and_1_out, Clock_out);  // AND_Gate
  Hex_Digit_Display hex_digit_display_1 (.value(Input[7:4]));  // open: dp
  and and_2 (and_2_out, Clock_out, RegSel[2]);
  and and_3 (and_3_out, Clock_out, RegSel[1]);
  Hex_Digit_Display hex_digit_display_2 (.value(Input[3:0]));  // open: dp
  and and_4 (and_4_out, Clock_out, RegSel[3]);
  _8_bit_register_main R0 (
    .Select1(FunSel[1]), .Select0(FunSel[0]), .Enable(and_4_out), .LSB_2(R0_lsb_2), .out_13(R0_out_13),
    .out_14(R0_out_14), .out_15(R0_out_15), .out_16(R0_out_16), .out_17(R0_out_17), .out_18(R0_out_18),
    .out_19(R0_out_19), .LSB(Input[0]), .in_5(Input[1]), .in_6(Input[2]), .in_7(Input[3]), .in_8(Input[4]),
    .in_9(Input[5]), .in_10(Input[6]), .in_11(Input[7]), .out_20(R0_out_20), .out_21(R0_out_21));  // open: out_22
  _8_bit_register_main R1 (
    .Select1(R0_out_20), .Select0(R0_out_21), .Enable(and_2_out), .LSB_2(R1_lsb_2), .out_13(R1_out_13),
    .out_14(R1_out_14), .out_15(R1_out_15), .out_16(R1_out_16), .out_17(R1_out_17), .out_18(R1_out_18),
    .out_19(R1_out_19), .LSB(Input[0]), .in_5(Input[1]), .in_6(Input[2]), .in_7(Input[3]), .in_8(Input[4]),
    .in_9(Input[5]), .in_10(Input[6]), .in_11(Input[7]), .out_20(R1_out_20), .out_21(R1_out_21));  // open: out_22
  _8_bit_register_main R2 (
    .Select1(R1_out_20), .Select0(R1_out_21), .Enable(and_3_out), .LSB_2(R2_lsb_2), .out_13(R2_out_13),
    .out_14(R2_out_14), .out_15(R2_out_15), .out_16(R2_out_16), .out_17(R2_out_17), .out_18(R2_out_18),
    .out_19(R2_out_19), .LSB(Input[0]), .in_5(Input[1]), .in_6(Input[2]), .in_7(Input[3]), .in_8(Input[4]),
    .in_9(Input[5]), .in_10(Input[6]), .in_11(Input[7]), .out_20(R2_out_20), .out_21(R2_out_21));  // open: out_22
  _8_bit_register_main R3 (
    .Select1(R2_out_20), .Select0(R2_out_21), .Enable(and_1_out), .LSB_2(R3_lsb_2), .out_13(R3_out_13),
    .out_14(R3_out_14), .out_15(R3_out_15), .out_16(R3_out_16), .out_17(R3_out_17), .out_18(R3_out_18),
    .out_19(R3_out_19), .LSB(Input[0]), .in_5(Input[1]), .in_6(Input[2]), .in_7(Input[3]), .in_8(Input[4]),
    .in_9(Input[5]), .in_10(Input[6]), .in_11(Input[7]));  // open: out_20, out_21, out_22
  _4_main main_1 (
    .in_1(R0_out_19), .in_2(R1_out_19), .in_3(R2_out_19), .in_4(R3_out_19), .out_9(outA[7]),
    .in_5(main_2_out_7), .in_6(main_2_out_8));  // open: out_7, out_8
  _4_main main_2 (
    .out_7(main_2_out_7), .out_8(main_2_out_8), .in_1(R0_out_18), .in_2(R1_out_18), .in_3(R2_out_18),
    .in_4(R3_out_18), .out_9(outA[6]), .in_5(main_3_out_7), .in_6(main_3_out_8));
  _4_main main_3 (
    .out_7(main_3_out_7), .out_8(main_3_out_8), .in_1(R0_out_17), .in_2(R1_out_17), .in_3(R2_out_17),
    .in_4(R3_out_17), .out_9(outA[5]), .in_5(main_4_out_7), .in_6(main_4_out_8));
  _4_main main_4 (
    .out_7(main_4_out_7), .out_8(main_4_out_8), .in_1(R0_out_16), .in_2(R1_out_16), .in_3(R2_out_16),
    .in_4(R3_out_16), .out_9(outA[4]), .in_5(main_5_out_7), .in_6(main_5_out_8));
  _4_main main_5 (
    .out_7(main_5_out_7), .out_8(main_5_out_8), .in_1(R0_out_15), .in_2(R1_out_15), .in_3(R2_out_15),
    .in_4(R3_out_15), .out_9(outA[3]), .in_5(main_6_out_7), .in_6(main_6_out_8));
  _4_main main_6 (
    .out_7(main_6_out_7), .out_8(main_6_out_8), .in_1(R0_out_14), .in_2(R1_out_14), .in_3(R2_out_14),
    .in_4(R3_out_14), .out_9(outA[2]), .in_5(main_7_out_7), .in_6(main_7_out_8));
  _4_main main_7 (
    .out_7(main_7_out_7), .out_8(main_7_out_8), .in_1(R0_out_13), .in_2(R1_out_13), .in_3(R2_out_13),
    .in_4(R3_out_13), .out_9(outA[1]), .in_5(main_8_out_7), .in_6(main_8_out_8));
  _4_main main_8 (
    .out_7(main_8_out_7), .out_8(main_8_out_8), .in_1(R0_lsb_2), .in_2(R1_lsb_2), .in_3(R2_lsb_2),
    .in_4(R3_lsb_2), .out_9(outA[0]), .in_5(OutASel[1]), .in_6(OutASel[0]));
  _4_main main_9 (
    .in_1(R0_out_19), .in_2(R1_out_19), .in_3(R2_out_19), .in_4(R3_out_19), .out_9(outB[7]),
    .in_5(main_10_out_7), .in_6(main_10_out_8));  // open: out_7, out_8
  _4_main main_10 (
    .out_7(main_10_out_7), .out_8(main_10_out_8), .in_1(R0_out_18), .in_2(R1_out_18), .in_3(R2_out_18),
    .in_4(R3_out_18), .out_9(outB[6]), .in_5(main_11_out_7), .in_6(main_11_out_8));
  _4_main main_11 (
    .out_7(main_11_out_7), .out_8(main_11_out_8), .in_1(R0_out_17), .in_2(R1_out_17), .in_3(R2_out_17),
    .in_4(R3_out_17), .out_9(outB[5]), .in_5(main_12_out_7), .in_6(main_12_out_8));
  _4_main main_12 (
    .out_7(main_12_out_7), .out_8(main_12_out_8), .in_1(R0_out_16), .in_2(R1_out_16), .in_3(R2_out_16),
    .in_4(R3_out_16), .out_9(outB[4]), .in_5(main_13_out_7), .in_6(main_13_out_8));
  _4_main main_13 (
    .out_7(main_13_out_7), .out_8(main_13_out_8), .in_1(R0_out_15), .in_2(R1_out_15), .in_3(R2_out_15),
    .in_4(R3_out_15), .out_9(outB[3]), .in_5(main_14_out_7), .in_6(main_14_out_8));
  _4_main main_14 (
    .out_7(main_14_out_7), .out_8(main_14_out_8), .in_1(R0_out_14), .in_2(R1_out_14), .in_3(R2_out_14),
    .in_4(R3_out_14), .out_9(outB[2]), .in_5(main_15_out_7), .in_6(main_15_out_8));
  _4_main main_15 (
    .out_7(main_15_out_7), .out_8(main_15_out_8), .in_1(R0_out_13), .in_2(R1_out_13), .in_3(R2_out_13),
    .in_4(R3_out_13), .out_9(outB[1]), .in_5(main_16_out_7), .in_6(main_16_out_8));
  _4_main main_16 (
    .out_7(main_16_out_7), .out_8(main_16_out_8), .in_1(R0_lsb_2), .in_2(R1_lsb_2), .in_3(R2_lsb_2),
    .in_4(R3_lsb_2), .out_9(outB[0]), .in_5(OutBSel[1]), .in_6(OutBSel[0]));
  Hex_Digit_Display hex_digit_display_3 (.value(outA[7:4]));  // open: dp
  Hex_Digit_Display hex_digit_display_4 (.value(outB[7:4]));  // open: dp
  Hex_Digit_Display hex_digit_display_5 (.value(outA[3:0]));  // open: dp
  Hex_Digit_Display hex_digit_display_6 (.value(outB[3:0]));  // open: dp
endmodule
