// Logisim project HW2main.circ as structural Verilog: 1 circuit, main circuit main
module main (
  input  [3:0] FunSel,
  input  [3:0] RegSel,
  input  [1:0] FunSel_2,
  input  [1:0] outAsel,
  input  [1:0] outBsel,
  input  [1:0] OutASel_2,
  input  [1:0] in_7,
  input  [1:0] FunSel_3,
  input  L_H_Select,
  input  [1:0] FunSel_4,
  input  [1:0] MuxBSel,
  input  [2:0] RegSel_2,
  output [3:0] ZCNO_Register,
  output [7:0] Output,
  output [3:0] ZCNO
);

  wire clock_1_out;
  wire [7:0] bit_extender_1_out, main_1_outa, main_1_outb, main_2_outa, multiplexer_1_out, multiplexer_2_out;
  wire [15:0] main_4_out_5;

  _4_registers_main main_1 (
    .FunSel(FunSel_2), .RegSel(RegSel), .Input(multiplexer_1_out), .OutASel(outAsel), .OutBSel(outBsel),
    .outA(main_1_outa), .outB(main_1_outb));
  D_Flip_Flop d_ff_1 (.D(ZCNO[3]), .Q(ZCNO_Register[3]), .en(clock_1_out));  // open: clk, Qn, preset, reset
  D_Flip_Flop d_ff_2 (.D(ZCNO[2]), .Q(ZCNO_Register[2]), .en(clock_1_out));  // open: clk, Qn, preset, reset
  _3_registers_main main_2 (
    .FunSel(FunSel_4), .RegSel(RegSel_2), .Input(multiplexer_2_out), .OutASel(OutASel_2), .outA(main_2_outa));
  D_Flip_Flop d_ff_3 (.D(ZCNO[1]), .Q(ZCNO_Register[1]), .en(clock_1_out));  // open: clk, Qn, preset, reset
  alu_main main_3 (
    .FunSel(FunSel), .Cin(ZCNO_Register[2]), .A(main_1_outa), .B(main_1_outb), .Output(Output), .ZCNO(ZCNO));
  D_Flip_Flop d_ff_4 (.D(ZCNO[0]), .Q(ZCNO_Register[0]), .en(clock_1_out));  // open: clk, Qn, preset, reset
  Multiplexer #(.select(2), .width(8), .enable("false")) multiplexer_1 (
    .in0(Output), .in1(Output), .in2(Output), .in3(bit_extender_1_out), .out(multiplexer_1_out), .sel(in_7));
  Multiplexer #(.select(2), .width(8), .enable("false")) multiplexer_2 (
    .in0(Output), .in2(Output), .in3(bit_extender_1_out), .out(multiplexer_2_out), .sel(MuxBSel));  // open: in1
  RAM ram_1 (.addr(main_2_outa), .data(Output));  // open: sel, clk, ld, clr
  Clock clock_1 (.out(clock_1_out));
  Bit_Extender #(.in_width(16), .out_width(8)) bit_extender_1 (.in(main_4_out_5), .out(bit_extender_1_out));
  _16_bit_IR_register_main main_4 (
    .out_5(main_4_out_5), .Enable(clock_1_out), .Funcel(FunSel_3), .L1_H0(L_H_Select), .in_4(Output));

  // Notes on the sheet:
  //   Part2a-4registers
  //   Address
  //   Part2b-3registers
  //   ALU
  //   MuxASel
  //   MuxA
  //   MuxB
  //   Part2c-16bitIRRegister
endmodule
