// Logisim project adder with overflow.circ as structural Verilog: 1 circuit, main circuit main
module main (
  input  Cin,
  input  [7:0] A,
  input  [7:0] B,
  output [7:0] Output,
  output Carry,
  output Overflow
);

  wire adder_1_cout;

  Adder #(.width(7)) adder_1 (.a(A[6:0]), .b(B[6:0]), .out(Output[6:0]), .cin(Cin), .cout(adder_1_cout));
  Adder #(.width(1)) adder_2 (.a(A[7]), .b(B[7]), .out(Output[7]), .cin(adder_1_cout), .cout(Carry));
  xor xor_1 (Overflow, Carry, adder_1_cout);
endmodule
