// Logisim project alu.circ as structural Verilog: 1 circuit, main circuit main
module main (
  input  [3:0] FunSel,
  input  Cin,
  input  [7:0] A,
  input  [7:0] B,
  output [7:0] Output,
  output [3:0] ZCNO
);

  wire or_2_out;
  wire [0:0] undriven, undriven_2, xor_4_out, xor_5_out;
  wire [1:0] main_1_overflow, main_2_overflow, main_3_overflow, xor_3_out;
  wire [7:0] and_1_out, main_1_output, main_2_output, main_3_output, not_1_out, not_2_out, or_1_out,
       xor_1_out, xor_2_out;

  assign xor_1_out = B ^ {8{1'b1}};  // XOR_Gate xor_1, 8 bits wide
  adder_with_overflow_main main_1 (
    .A(A), .B(B), .Cin(Cin), .Output(main_1_output), .Carry(main_1_overflow[1]), .Overflow(main_1_overflow[0]));
  adder_with_overflow_main main_2 (
    .A(A), .B(B), .Output(main_2_output), .Carry(main_2_overflow[1]), .Overflow(main_2_overflow[0]));  // open: Cin
  adder_with_overflow_main main_3 (
    .A(A), .B(xor_1_out), .Cin(1'b1), .Output(main_3_output), .Carry(main_3_overflow[1]),
    .Overflow(main_3_overflow[0]));
  assign and_1_out = A & B;  // AND_Gate and_1, 8 bits wide
  assign or_1_out = A | B;  // OR_Gate or_1, 8 bits wide
  assign not_1_out = ~A;  // NOT_Gate not_1, 8 bits wide
  assign xor_2_out = A ^ B;  // XOR_Gate xor_2, 8 bits wide
  assign not_2_out = ~B;  // NOT_Gate not_2, 8 bits wide
  xor xor_3 (xor_3_out[0], A[6], A[7]);
  xor xor_4 (xor_4_out[0], Cin, A[7]);
  xor xor_5 (xor_5_out[0], A[7], A[6]);
  Multiplexer #(.select(4), .width(8), .disabled(0), .enable("false")) multiplexer_1 (
    .in0(A), .in1(main_2_output), .in2(main_1_output), .in3(main_3_output), .in4(and_1_out), .in5(or_1_out),
    .in6(not_1_out), .in7(xor_2_out), .in8({A[6:0], 1'b0}), .in9({1'b0, A[7:1]}), .in10({A[6:0], 1'b0}),
    .in11({{2{A[7]}}, A[6:1]}), .in12({Cin, A[7:1]}), .in13({A[6:0], Cin}), .in14(B), .in15(not_2_out),
    .out(Output), .sel(FunSel));
  Multiplexer #(.select(4), .width(2)) multiplexer_2 (
    .in1(main_1_overflow), .in2(main_2_overflow), .in3(main_3_overflow), .in8({A[7], undriven[0]}),
    .in9({A[0], undriven_2[0]}), .in10(xor_3_out), .in11({A[0], 1'b0}), .in12({A[0], xor_4_out[0]}),
    .in13({A[7], xor_5_out[0]}), .out({ZCNO[2], ZCNO[0]}), .sel(FunSel));  // open: in0, in4, in5, in6, in7, in14, in15, en
  or or_2 (or_2_out, Output[7], Output[6], Output[5], Output[4], Output[3], Output[2], Output[1], Output[0]);
  not not_3 (ZCNO[3], or_2_out);
  Multiplexer #(.select(4)) multiplexer_3 (
    .in0(Output[7]), .in1(Output[7]), .in2(Output[7]), .in3(Output[7]), .in4(Output[7]), .in5(Output[7]),
    .in6(Output[7]), .in7(Output[7]), .in8(Output[7]), .in9(Output[7]), .in10(Output[7]), .in12(Output[7]),
    .in13(Output[7]), .in14(Output[7]), .in15(Output[7]), .out(ZCNO[1]), .sel(FunSel));  // open: in11, en
endmodule
