// Logisim project hw3.circ as structural Verilog: 1 circuit, main circuit main
module main (
  input  A,
  input  B,
  input  C,
  input  D,
  output out_5
);

  wire nor_1_out, nor_2_out, nor_3_out, nor_4_out, nor_5_out, nor_6_out, nor_7_out;

  nor nor_1 (nor_1_out, A, A);
  nor nor_2 (nor_2_out, B, C);
  nor nor_3 (nor_3_out, C, A);
  nor nor_4 (nor_4_out, nor_1_out, D);
  nor nor_5 (nor_5_out, nor_4_out, nor_2_out);
  nor nor_6 (nor_6_out, nor_5_out, nor_5_out);
  nor nor_7 (nor_7_out, nor_6_out, nor_3_out);
  nor nor_8 (out_5, nor_7_out, nor_7_out);
endmodule
