// Logisim project hw5_ninova.circ as structural Verilog: 1 circuit, main circuit main
module main (
  input  A,
  input  B,
  output Success,
  output Error
);

  wire and_1_out, and_2_out, and_3_out, and_4_out, and_5_out, and_6_out, and_7_out, and_8_out, and_9_out,
       and_10_out, and_11_out, Clock_out, decoder_1_out0, decoder_1_out1, decoder_1_out2, decoder_1_out3,
       decoder_2_out0, decoder_2_out1, decoder_2_out2, decoder_2_out3, not_1_out, not_2_out, or_1_out,
       or_2_out, or_3_out, or_4_out, or_5_out, or_6_out, or_7_out, Q0, Q1, Q2;

  Decoder #(.select(2), .enable("false")) decoder_1 (
    .out0(decoder_1_out0), .out1(decoder_1_out1), .out2(decoder_1_out2), .out3(decoder_1_out3), .sel({Q1, Q0}));
  Decoder #(.select(2), .enable("false")) decoder_2 (
    .out0(decoder_2_out0), .out1(decoder_2_out1), .out2(decoder_2_out2), .out3(decoder_2_out3), .sel({A, B}));
  and and_1 (and_1_out, A, Q2);
  and and_2 (and_2_out, Q2, not_1_out);
  not not_1 (not_1_out, A);
  or or_1 (or_1_out, decoder_2_out2, decoder_2_out1);
  and and_3 (and_3_out, or_1_out, Q2);
  and and_4 (and_4_out, decoder_1_out2, and_1_out);
  and and_5 (and_5_out, decoder_1_out1, and_2_out);
  or or_2 (or_2_out, and_3_out, decoder_1_out3);
  and and_6 (and_6_out, Q2, Q1);
  and and_7 (and_7_out, decoder_2_out3, decoder_1_out2);
  or or_3 (or_3_out, decoder_2_out3, decoder_2_out0, decoder_1_out3);
  and and_8 (and_8_out, or_3_out, Q2);
  and and_9 (and_9_out, Q2, Q0);
  and and_10 (and_10_out, decoder_2_out3, or_4_out);
  or or_4 (or_4_out, and_6_out, decoder_1_out1);
  and and_11 (and_11_out, decoder_2_out3, decoder_1_out0);
  or or_5 (or_5_out, and_7_out, and_8_out);
  or or_6 (or_6_out, or_2_out, and_9_out, and_10_out);
  or or_7 (or_7_out, or_2_out, and_11_out, and_4_out, and_5_out);
  Clock Clock (.out(Clock_out));
  D_Flip_Flop u_Q2 (.clk(Clock_out), .D(or_5_out), .Q(Q2));  // open: Qn, preset, en, reset
  D_Flip_Flop u_Q1 (.clk(Clock_out), .D(or_6_out), .Q(Q1));  // open: Qn, preset, en, reset
  D_Flip_Flop u_Q0 (.clk(Clock_out), .D(or_7_out), .Q(Q0));  // open: Qn, preset, en, reset
  and and_12 (Success, Q0, Q1, Q2);
  and and_13 (Error, Q0, Q1, not_2_out);
  not not_2 (not_2_out, Q2);
endmodule
