// Logisim project lab1.circ as structural Verilog: 1 circuit, main circuit main
module main (
  input  A,
  input  B,
  input  C,
  input  [2:0] in_4,
  output out_5,
  output out_6
);

  wire adder_1_cout, adder_1_out, adder_2_cout, adder_2_out, not_1_out, not_2_out, xor_1_out, xor_2_out;

  not not_1 (not_1_out, B);
  Adder #(.width(1)) adder_1 (.a(A), .b(B), .out(adder_1_out), .cin(C), .cout(adder_1_cout));
  Adder #(.width(1)) adder_2 (.a(A), .b(not_1_out), .out(adder_2_out), .cin(C), .cout(adder_2_cout));
  xor xor_1 (xor_1_out, A, B);
  not not_2 (not_2_out, A);
  xor xor_2 (xor_2_out, not_2_out, C);
  Multiplexer #(.enable("false")) multiplexer_1 (.in0(adder_1_cout), .in1(adder_2_cout), .out(out_5), .sel(in_4[0]));
  Multiplexer #(.select(3), .enable("false")) multiplexer_2 (
    .in0(adder_1_out), .in1(adder_2_out), .in2(xor_1_out), .in3(1'b0), .in4(not_2_out), .in5(xor_2_out),
    .in6(B), .out(out_6), .sel(in_4));  // open: in7
endmodule
