// Logisim project lab2.circ as structural Verilog: 1 circuit, main circuit main
module main (
  input  A,
  input  B,
  input  [2:0] FunSel,
  output [3:0] Output
);

  wire Clock_out, d_ff_2_q, main_1_out_5, main_1_out_6;

  Clock Clock (.out(Clock_out));
  lab3_main main_1 (.A(A), .B(B), .C(d_ff_2_q), .in_4(FunSel), .out_6(main_1_out_6), .out_5(main_1_out_5));
  D_Flip_Flop d_ff_1 (.clk(Clock_out), .D(main_1_out_6), .Q(Output[3]));  // open: Qn, preset, en, reset
  D_Flip_Flop d_ff_2 (.clk(Clock_out), .D(main_1_out_5), .Q(d_ff_2_q));  // open: Qn, preset, en, reset
  D_Flip_Flop d_ff_3 (.clk(Clock_out), .D(Output[3]), .Q(Output[2]));  // open: Qn, preset, en, reset
  D_Flip_Flop d_ff_4 (.clk(Clock_out), .D(Output[2]), .Q(Output[1]));  // open: Qn, preset, en, reset
  D_Flip_Flop d_ff_5 (.clk(Clock_out), .D(Output[1]), .Q(Output[0]));  // open: Qn, preset, en, reset
  Hex_Digit_Display hex_digit_display_1 (.value(Output));  // open: dp
endmodule
