// Logisim project lab3.circ as structural Verilog: 1 circuit, main circuit main
module main (
  input  A,
  input  B,
  input  C,
  input  [2:0] in_4,
  output out_5,
  output out_6
);

  wire and_1_out, and_2_out, not_1_out, xor_1_out, xor_2_out, xor_3_out, xor_4_out;

  and and_1 (and_1_out, A, B);
  xor xor_1 (xor_1_out, A, xor_2_out);
  not not_1 (not_1_out, A);
  xor xor_2 (xor_2_out, in_4[0], B);
  xor xor_3 (xor_3_out, C, xor_1_out);
  xor xor_4 (xor_4_out, not_1_out, C);
  or or_1 (out_5, and_1_out, and_2_out);
  and and_2 (and_2_out, C, xor_1_out);
  Multiplexer #(.select(3), .enable("false")) multiplexer_1 (
    .in0(xor_3_out), .in1(xor_3_out), .in2(xor_1_out), .in3(1'b0), .in4(not_1_out), .in5(xor_4_out), .in6(B),
    .out(out_6), .sel(in_4));  // open: in7
endmodule
