// Logisim project lab4.circ as structural Verilog: 1 circuit, main circuit main
module main (
  input  C,
  input  A,
  input  B,
  input  [2:0] in_4,
  output out_5,
  output out_6
);

  wire adder_1_out, xor_1_out, xor_2_out, xor_3_out, xor_4_out;

  xor xor_1 (xor_1_out, B, in_4[0]);
  Adder #(.width(1)) adder_1 (.a(A), .b(xor_1_out), .out(adder_1_out), .cin(C), .cout(out_5));
  xor xor_2 (xor_2_out, A, B);
  xor xor_3 (xor_3_out, A, 1'b1);
  xor xor_4 (xor_4_out, xor_3_out, C);
  Multiplexer #(.select(3), .enable("false")) multiplexer_1 (
    .in0(adder_1_out), .in1(adder_1_out), .in2(xor_2_out), .in3(1'b0), .in4(xor_3_out), .in5(xor_4_out),
    .in6(B), .out(out_6), .sel(in_4));  // open: in7
endmodule
