// Logisim project CİRCUİT.circ as structural Verilog: 1 circuit, main circuit main
module main (
  input  [7:0] VNB1,
  input  [7:0] VNB2,
  input  IRQB1,
  input  IRQB2,
  input  INTA,
  input  IRQA1,
  input  IRQA2,
  output INTAB1,
  output INTAB2,
  output IRQ,
  output VA,
  output [7:0] VN,
  output DACK,
  output INTAA1,
  output INTAA2
);

  wire and_2_out, and_4_out, and_6_out;
  wire [7:0] and_8_out, and_9_out;

  and and_1 (INTAA1, INTA, IRQA1);
  and and_2 (and_2_out, ~IRQB1, and_6_out);  // AND_Gate
  and and_3 (INTAB1, IRQB1, and_6_out);
  and and_4 (and_4_out, ~IRQA1, INTA);  // AND_Gate
  and and_5 (INTAB2, IRQB2, and_2_out);
  and and_6 (and_6_out, ~IRQA2, and_4_out);  // AND_Gate
  and and_7 (INTAA2, and_4_out, IRQA2);
  nor nor_1 (VA, INTAB1, INTAB2);
  assign and_8_out = VNB1 & {8{INTAB1}};  // AND_Gate and_8, 8 bits wide
  or or_1 (IRQ, IRQB2, IRQB1, IRQA1, IRQA2);
  assign and_9_out = VNB2 & {8{INTAB2}};  // AND_Gate and_9, 8 bits wide
  assign VN = and_8_out | and_9_out;  // OR_Gate or_2, 8 bits wide
  not not_1 (DACK, VA);
endmodule
